// Logisim project combinational_blocks.circ as structural Verilog: 24 circuits, main circuit half_adder_1bit
module half_adder_1bit (
  input  A,
  input  B,
  output S,
  output Co
);

  and and_1 (Co, A, B);
  xor xor_1 (S, A, B);

  // Notes on the sheet:
  //   1-bit Half Adder
endmodule

module full_adder_1bit (
  input  Ci,
  input  A,
  input  B,
  output S,
  output Co
);

  wire and_1_out, and_2_out, and_3_out, xor_1_out;

  and and_1 (and_1_out, Ci, B);
  and and_2 (and_2_out, A, B);
  and and_3 (and_3_out, A, Ci);
  xor xor_1 (xor_1_out, A, B);
  xor xor_2 (S, Ci, xor_1_out);
  or or_1 (Co, and_1_out, and_2_out, and_3_out);

  // Notes on the sheet:
  //   1-bit Full Adder
endmodule

module full_adder_1_bit_alt (
  input  Ci,
  input  A,
  input  B,
  output S,
  output Co
);

  wire _1_bit_Half_Adder_2_co, _1_bit_Half_Adder_co, _1_bit_Half_Adder_s;

  half_adder_1bit _1_bit_Half_Adder (.A(A), .S(_1_bit_Half_Adder_s), .B(B), .Co(_1_bit_Half_Adder_co));
  half_adder_1bit _1_bit_Half_Adder_2 (.A(Ci), .S(S), .B(_1_bit_Half_Adder_s), .Co(_1_bit_Half_Adder_2_co));
  or or_1 (Co, _1_bit_Half_Adder_2_co, _1_bit_Half_Adder_co);

  // Notes on the sheet:
  //   1-bit Full Adder (Alternative)
endmodule

module ripple_carry_4bit_adder (
  input  Ci,
  input  A0,
  input  B0,
  input  A1,
  input  B1,
  input  A2,
  input  B2,
  input  A3,
  input  B3,
  output S0,
  output S1,
  output S2,
  output S3,
  output C4
);

  wire full_adder_1bit_1_co, full_adder_1bit_2_co, full_adder_1bit_3_co;

  full_adder_1bit full_adder_1bit_1 (.Ci(Ci), .A(A0), .B(B0), .S(S0), .Co(full_adder_1bit_1_co));
  full_adder_1bit full_adder_1bit_2 (.Ci(full_adder_1bit_1_co), .A(A1), .B(B1), .S(S1), .Co(full_adder_1bit_2_co));
  full_adder_1bit full_adder_1bit_3 (.Ci(full_adder_1bit_2_co), .A(A2), .B(B2), .S(S2), .Co(full_adder_1bit_3_co));
  full_adder_1bit full_adder_1bit_4 (.Ci(full_adder_1bit_3_co), .A(A3), .B(B3), .S(S3), .Co(C4));

  // Notes on the sheet:
  //   4-bit Ripple-Carry Adder
  //   When the most significant nibble → C4 = Overflow Flag
endmodule

module cascate_8bit_adder (
  input  C0,
  input  A0,
  input  B0,
  input  A1,
  input  B1,
  input  A2,
  input  B2,
  input  A3,
  input  B3,
  input  A4,
  input  B4,
  input  A5,
  input  B5,
  input  A6,
  input  B6,
  input  A7,
  input  B7,
  output S0,
  output S1,
  output S2,
  output S3,
  output S4,
  output S5,
  output S6,
  output S7,
  output C8
);

  wire ripple_carry_4bit_adder_1_c4;

  ripple_carry_4bit_adder ripple_carry_4bit_adder_1 (
    .Ci(C0), .A0(A0), .B0(B0), .A1(A1), .B1(B1), .A2(A2), .B2(B2), .A3(A3), .B3(B3), .S0(S0), .S1(S1),
    .S2(S2), .S3(S3), .C4(ripple_carry_4bit_adder_1_c4));
  ripple_carry_4bit_adder ripple_carry_4bit_adder_2 (
    .Ci(ripple_carry_4bit_adder_1_c4), .A0(A4), .B0(B4), .A1(A5), .B1(B5), .A2(A6), .B2(B6), .A3(A7),
    .B3(B7), .S0(S4), .S1(S5), .S2(S6), .S3(S7), .C4(C8));

  // Notes on the sheet:
  //   8-bit Cascate Adder
  //   When the most significant byte → C8 = Overflow Flag
endmodule

module half_subtractor_1bit (
  input  A,
  input  B,
  output S,
  output To
);

  wire not_1_out;

  not not_1 (not_1_out, A);
  xor xor_1 (S, B, A);
  and and_1 (To, not_1_out, B);

  // Notes on the sheet:
  //   1-bit Half Subtractor
endmodule

module full_subtractor_1bit (
  input  Ti,
  input  A,
  input  B,
  output S,
  output To
);

  wire and_1_out, and_2_out, and_3_out, not_1_out, xor_1_out;

  not not_1 (not_1_out, A);
  xor xor_1 (xor_1_out, A, B);
  and and_1 (and_1_out, Ti, not_1_out);
  and and_2 (and_2_out, not_1_out, B);
  and and_3 (and_3_out, B, Ti);
  xor xor_2 (S, Ti, xor_1_out);
  or or_1 (To, and_1_out, and_2_out, and_3_out);

  // Notes on the sheet:
  //   1-bit Full Subtractor
endmodule

module full_subtractor_alt_1bit (
  input  Ti,
  input  A,
  input  B,
  output S,
  output To
);

  wire _1_bit_Half_Subtractor_2_p5, _1_bit_Half_Subtractor_p3, _1_bit_Half_Subtractor_p4;

  // half_subtractor_1bit _1_bit_Half_Subtractor: pin names not known; wires that end beside it: A, B, _1_bit_Half_Subtractor_p3, _1_bit_Half_Subtractor_p4
  // half_subtractor_1bit _1_bit_Half_Subtractor_2: pin names not known; wires that end beside it: _1_bit_Half_Subtractor_p3, _1_bit_Half_Subtractor_p3, Ti, S, _1_bit_Half_Subtractor_2_p5
  or or_1 (To, _1_bit_Half_Subtractor_2_p5, _1_bit_Half_Subtractor_p4);

  // Notes on the sheet:
  //   1-bit Full Subtractor (Alternative)
endmodule

module ripple_borrow_4bit_subtractor (
  input  T0,
  input  A0,
  input  B0,
  input  A1,
  input  B1,
  input  A2,
  input  B2,
  input  A3,
  input  B3,
  output S0,
  output S1,
  output S2,
  output S3,
  output T4
);

  wire _1_bit_Full_Subtractor_2_to, _1_bit_Full_Subtractor_3_to, _1_bit_Full_Subtractor_to;

  full_subtractor_1bit _1_bit_Full_Subtractor (.Ti(T0), .A(A0), .B(B0), .S(S0), .To(_1_bit_Full_Subtractor_to));
  full_subtractor_1bit _1_bit_Full_Subtractor_2 (
    .Ti(_1_bit_Full_Subtractor_to), .A(A1), .B(B1), .S(S1), .To(_1_bit_Full_Subtractor_2_to));
  full_subtractor_1bit _1_bit_Full_Subtractor_3 (
    .Ti(_1_bit_Full_Subtractor_2_to), .A(A2), .B(B2), .S(S2), .To(_1_bit_Full_Subtractor_3_to));
  full_subtractor_1bit _1_bit_Full_Subtractor_4 (.Ti(_1_bit_Full_Subtractor_3_to), .A(A3), .B(B3), .S(S3), .To(T4));

  // Notes on the sheet:
  //   4-bit Ripple-Borrow Subtractor
endmodule

module cascade_8bit_subtractor (
  input  T0,
  input  A0,
  input  B0,
  input  A1,
  input  B1,
  input  A2,
  input  B2,
  input  A3,
  input  B3,
  input  A4,
  input  B4,
  input  A5,
  input  B5,
  input  A6,
  input  B6,
  input  A7,
  input  B7,
  output S0,
  output S1,
  output S2,
  output S3,
  output S4,
  output S5,
  output S6,
  output S7,
  output T8
);

  wire _4_bit_Ripple_Borrow_Subtractor_t4;

  ripple_borrow_4bit_subtractor _4_bit_Ripple_Borrow_Subtractor (
    .T0(T0), .A0(A0), .B0(B0), .A1(A1), .B1(B1), .A2(A2), .B2(B2), .A3(A3), .B3(B3), .S0(S0), .S1(S1),
    .S2(S2), .S3(S3), .T4(_4_bit_Ripple_Borrow_Subtractor_t4));
  ripple_borrow_4bit_subtractor _4_bit_Ripple_Borrow_Subtractor_2 (
    .T0(_4_bit_Ripple_Borrow_Subtractor_t4), .A0(A4), .B0(B4), .A1(A5), .B1(B5), .A2(A6), .B2(B6), .A3(A7),
    .B3(B7), .S0(S4), .S1(S5), .S2(S6), .S3(S7), .T4(T8));

  // Notes on the sheet:
  //   8-bit Cascate Subtractor
endmodule

module complement_4bit_subtractor (
  input  C0,
  input  A0,
  input  B0,
  input  A1,
  input  B1,
  input  A2,
  input  B2,
  input  A3,
  input  B3,
  output S0,
  output S1,
  output S2,
  output S3,
  output C4
);

  wire not_1_out, not_2_out, not_3_out, not_4_out;

  not not_1 (not_1_out, B0);
  not not_2 (not_2_out, B1);
  not not_3 (not_3_out, B2);
  not not_4 (not_4_out, B3);
  ripple_carry_4bit_adder ripple_carry_4bit_adder_1 (
    .Ci(C0), .A0(A0), .B0(not_1_out), .A1(A1), .B1(not_2_out), .A2(A2), .B2(not_3_out), .A3(A3),
    .B3(not_4_out), .S0(S0), .S1(S1), .S2(S2), .S3(S3), .C4(C4));

  // Notes on the sheet:
  //   4-bit Two's Complement Subtractor
endmodule

module controlled_4bit_adder_subtractor (
  input  Ci,
  input  M,
  input  A0,
  input  B0,
  input  A1,
  input  B1,
  input  A2,
  input  B2,
  input  A3,
  input  B3,
  output S0,
  output S1,
  output S2,
  output S3,
  output C4
);

  wire _1_bit_Full_Adder_2_co, _1_bit_Full_Adder_3_co, _1_bit_Full_Adder_co, or_1_out, xor_1_out, xor_2_out,
       xor_3_out, xor_4_out;

  or or_1 (or_1_out, Ci, M);
  xor xor_1 (xor_1_out, B0, M);
  xor xor_2 (xor_2_out, B1, M);
  xor xor_3 (xor_3_out, B2, M);
  xor xor_4 (xor_4_out, B3, M);
  full_adder_1bit _1_bit_Full_Adder (.Ci(or_1_out), .A(A0), .B(xor_1_out), .S(S0), .Co(_1_bit_Full_Adder_co));
  full_adder_1bit _1_bit_Full_Adder_2 (
    .Ci(_1_bit_Full_Adder_co), .A(A1), .B(xor_2_out), .S(S1), .Co(_1_bit_Full_Adder_2_co));
  full_adder_1bit _1_bit_Full_Adder_3 (
    .Ci(_1_bit_Full_Adder_2_co), .A(A2), .B(xor_3_out), .S(S2), .Co(_1_bit_Full_Adder_3_co));
  full_adder_1bit _1_bit_Full_Adder_4 (.Ci(_1_bit_Full_Adder_3_co), .A(A3), .B(xor_4_out), .S(S3), .Co(C4));

  // Notes on the sheet:
  //   4-bit Controlled Adder and Subtractor
  //   M = 0V -> SUM
  //   M = 5V -> SUB
endmodule

module incrementer_4bit (
  input  A0,
  input  A1,
  input  A2,
  input  A3,
  input  VSS,
  output S0,
  output S1,
  output S2,
  output S3,
  output C4
);

  wire half_adder_1bit_1_co, half_adder_1bit_2_co, half_adder_1bit_3_co;

  half_adder_1bit half_adder_1bit_1 (.A(A0), .S(S0), .B(VSS), .Co(half_adder_1bit_1_co));
  half_adder_1bit half_adder_1bit_2 (.A(A1), .S(S1), .B(half_adder_1bit_1_co), .Co(half_adder_1bit_2_co));
  half_adder_1bit half_adder_1bit_3 (.A(A2), .S(S2), .B(half_adder_1bit_2_co), .Co(half_adder_1bit_3_co));
  half_adder_1bit half_adder_1bit_4 (.A(A3), .S(S3), .B(half_adder_1bit_3_co), .Co(C4));

  // Notes on the sheet:
  //   4-bit Incrementer
endmodule

module decrementer_4bit (
  input  A0,
  input  A1,
  input  A2,
  input  A3,
  input  VSS,
  output S0,
  output S1,
  output S2,
  output S3,
  output C4
);

  wire half_subtractor_1bit_1_to, half_subtractor_1bit_2_to, half_subtractor_1bit_3_to;

  half_subtractor_1bit half_subtractor_1bit_1 (.A(A0), .B(VSS), .S(S0), .To(half_subtractor_1bit_1_to));
  half_subtractor_1bit half_subtractor_1bit_2 (
    .A(A1), .B(half_subtractor_1bit_1_to), .S(S1), .To(half_subtractor_1bit_2_to));
  half_subtractor_1bit half_subtractor_1bit_3 (
    .A(A2), .B(half_subtractor_1bit_2_to), .S(S2), .To(half_subtractor_1bit_3_to));
  half_subtractor_1bit half_subtractor_1bit_4 (.A(A3), .B(half_subtractor_1bit_3_to), .S(S3), .To(C4));

  // Notes on the sheet:
  //   4-bit Decrementer
endmodule

module bcd_4bit_adder (
  input  Ci,
  input  A0,
  input  B0,
  input  A1,
  input  B1,
  input  A2,
  input  B2,
  input  A3,
  input  B3,
  input  GND,
  output S0,
  output S1,
  output S2,
  output S3,
  output C4
);

  wire and_1_out, and_2_out, ripple_carry_4bit_adder_1_c4, ripple_carry_4bit_adder_1_s0,
       ripple_carry_4bit_adder_1_s1, ripple_carry_4bit_adder_1_s2, ripple_carry_4bit_adder_1_s3;

  ripple_carry_4bit_adder ripple_carry_4bit_adder_1 (
    .Ci(Ci), .A0(A0), .B0(B0), .A1(A1), .B1(B1), .A2(A2), .B2(B2), .A3(A3), .B3(B3),
    .S0(ripple_carry_4bit_adder_1_s0), .S1(ripple_carry_4bit_adder_1_s1), .S2(ripple_carry_4bit_adder_1_s2),
    .S3(ripple_carry_4bit_adder_1_s3), .C4(ripple_carry_4bit_adder_1_c4));
  and and_1 (and_1_out, ripple_carry_4bit_adder_1_s3, ripple_carry_4bit_adder_1_s2);
  or or_1 (C4, ripple_carry_4bit_adder_1_c4, and_1_out, and_2_out);
  and and_2 (and_2_out, ripple_carry_4bit_adder_1_s3, ripple_carry_4bit_adder_1_s1);
  ripple_carry_4bit_adder ripple_carry_4bit_adder_2 (
    .Ci(GND), .A0(ripple_carry_4bit_adder_1_s0), .B0(GND), .A1(ripple_carry_4bit_adder_1_s1), .B1(C4),
    .A2(ripple_carry_4bit_adder_1_s2), .B2(C4), .A3(ripple_carry_4bit_adder_1_s3), .B3(GND), .S0(S0),
    .S1(S1), .S2(S2), .S3(S3));  // open: C4

  // Notes on the sheet:
  //   4-bit BCD Adder
endmodule

module bcd_4bit_subtractor (
  input  Ci,
  input  A0,
  input  B0,
  input  A1,
  input  B1,
  input  A2,
  input  B2,
  input  A3,
  input  B3,
  input  GND,
  output S0,
  output S1,
  output S2,
  output S3,
  output C4
);

  wire not_1_out, not_2_out, not_4_out, not_5_out, not_6_out, ripple_carry_4bit_adder_1_s0,
       ripple_carry_4bit_adder_1_s1, ripple_carry_4bit_adder_1_s2, ripple_carry_4bit_adder_1_s3;

  not not_1 (not_1_out, B0);
  not not_2 (not_2_out, B1);
  not not_3 (not_2_out, B1);
  not not_4 (not_4_out, B2);
  not not_5 (not_5_out, B3);
  ripple_carry_4bit_adder ripple_carry_4bit_adder_1 (
    .Ci(Ci), .A0(A0), .B0(not_1_out), .A1(A1), .B1(not_2_out), .A2(A2), .B2(not_4_out), .A3(A3),
    .B3(not_5_out), .S0(ripple_carry_4bit_adder_1_s0), .S1(ripple_carry_4bit_adder_1_s1),
    .S2(ripple_carry_4bit_adder_1_s2), .S3(ripple_carry_4bit_adder_1_s3), .C4(C4));
  not not_6 (not_6_out, C4);
  ripple_carry_4bit_adder ripple_carry_4bit_adder_2 (
    .Ci(GND), .A0(ripple_carry_4bit_adder_1_s0), .B0(GND), .A1(ripple_carry_4bit_adder_1_s1), .B1(not_6_out),
    .A2(ripple_carry_4bit_adder_1_s2), .B2(GND), .A3(ripple_carry_4bit_adder_1_s3), .B3(not_6_out), .S0(S0),
    .S1(S1), .S2(S2), .S3(S3));  // open: C4

  // Notes on the sheet:
  //   Ci must be 5V
  //   4-bit BCD Subtractor
endmodule

module array_multiplier_2bit_2bit (
  input  A0,
  input  B0,
  input  A1,
  input  B1,
  output S0,
  output S1,
  output S2,
  output S3
);

  wire and_2_out, and_3_out, and_4_out, half_adder_1bit_1_co;

  and and_1 (S0, A0, B0);
  and and_2 (and_2_out, A0, B1);
  and and_3 (and_3_out, A1, B0);
  and and_4 (and_4_out, B1, A1);
  half_adder_1bit half_adder_1bit_1 (.A(and_2_out), .S(S1), .B(and_3_out), .Co(half_adder_1bit_1_co));
  half_adder_1bit half_adder_1bit_2 (.A(half_adder_1bit_1_co), .S(S2), .B(and_4_out), .Co(S3));

  // Notes on the sheet:
  //   2-bit X 2-bit Array Multiplier
endmodule

module magnitude_comparer_4bit (
  input  A3,
  input  B3,
  input  A2,
  input  B2,
  input  A1,
  input  B1,
  input  A0,
  input  B0,
  output Seq,
  output Slt,
  output Sgt
);

  wire and_1_out, and_2_out, and_3_out, and_4_out, not_1_out, not_2_out, not_3_out, not_4_out, xnor_1_out,
       xnor_2_out, xnor_3_out, xnor_4_out;

  xnor xnor_1 (xnor_1_out, A3, B3);
  not not_1 (not_1_out, B3);
  xnor xnor_2 (xnor_2_out, A2, B2);
  not not_2 (not_2_out, B2);
  xnor xnor_3 (xnor_3_out, A1, B1);
  not not_3 (not_3_out, B1);
  xnor xnor_4 (xnor_4_out, A0, B0);
  not not_4 (not_4_out, B0);
  and and_1 (and_1_out, A3, not_1_out);
  and and_2 (and_2_out, xnor_1_out, A2, not_2_out);
  and and_3 (and_3_out, xnor_1_out, xnor_2_out, A1, not_3_out);
  and and_4 (and_4_out, xnor_3_out, xnor_2_out, xnor_1_out, A0, not_4_out);
  and and_5 (Seq, xnor_1_out, xnor_2_out, xnor_3_out, xnor_4_out);
  nor nor_1 (Slt, Seq, Sgt);
  or or_1 (Sgt, and_1_out, and_2_out, and_3_out, and_4_out);

  // Notes on the sheet:
  //   4-bit Magnitude Comparator
endmodule

module carry_look_ahead_generator (
  input  G2,
  input  P2,
  input  G1,
  input  P1,
  input  G0,
  input  P0,
  input  Ci,
  output C3,
  output C2,
  output C1
);

  wire and_1_out, and_2_out, and_3_out, and_4_out, and_5_out, and_6_out;

  and and_1 (and_1_out, P2, G1);
  and and_2 (and_2_out, P2, P1, G0);
  and and_3 (and_3_out, P2, P1, P0, Ci);
  and and_4 (and_4_out, P1, G0);
  and and_5 (and_5_out, P1, P0, Ci);
  and and_6 (and_6_out, P0, Ci);
  or or_1 (C3, G2, and_1_out, and_2_out, and_3_out);
  or or_2 (C2, G1, and_4_out, and_5_out);
  or or_3 (C1, G0, and_6_out);

  // Notes on the sheet:
  //   Carry Look-Ahead Generator
endmodule

module carry_look_ahead_4bit_adder (
  input  A3,
  input  B3,
  input  A2,
  input  B2,
  input  A1,
  input  B1,
  input  A0,
  input  B0,
  input  Ci,
  output Co,
  output S3,
  output S2,
  output S1,
  output S0
);

  wire and_2_out, and_3_out, and_4_out, carry_look_ahead_generator_1_c1, carry_look_ahead_generator_1_c2,
       carry_look_ahead_generator_1_c3, xor_1_out, xor_2_out, xor_3_out, xor_4_out;

  xor xor_1 (xor_1_out, A3, B3);
  and and_1 (Co, A3, B3);
  xor xor_2 (xor_2_out, A2, B2);
  and and_2 (and_2_out, A2, B2);
  xor xor_3 (xor_3_out, A1, B1);
  and and_3 (and_3_out, A1, B1);
  xor xor_4 (xor_4_out, A0, B0);
  and and_4 (and_4_out, A0, B0);
  carry_look_ahead_generator carry_look_ahead_generator_1 (
    .P2(xor_2_out), .G1(and_3_out), .P1(xor_3_out), .G0(and_4_out), .P0(xor_4_out), .Ci(Ci),
    .C3(carry_look_ahead_generator_1_c3), .C2(carry_look_ahead_generator_1_c2),
    .C1(carry_look_ahead_generator_1_c1), .G2(and_2_out));
  xor xor_5 (S3, xor_1_out, carry_look_ahead_generator_1_c3);
  xor xor_6 (S2, xor_2_out, carry_look_ahead_generator_1_c2);
  xor xor_7 (S1, xor_3_out, carry_look_ahead_generator_1_c1);
  xor xor_8 (S0, xor_4_out, Ci);

  // Notes on the sheet:
  //   4-bit Carry Look-Ahead Adder
endmodule

module parity_4bit_generator (
  input  B3,
  input  B2,
  input  B1,
  input  B0,
  output P
);

  wire xor_1_out, xor_2_out;

  xor xor_1 (xor_1_out, B3, B2);
  xor xor_2 (xor_2_out, xor_1_out, B1);
  xor xor_3 (P, xor_2_out, B0);
endmodule

module parity_4bit_verifier (
  input  B3,
  input  B2,
  input  B1,
  input  B0,
  input  P,
  output E
);

  wire parity_4bit_generator_1_p;

  parity_4bit_generator parity_4bit_generator_1 (.B3(B3), .B2(B2), .B1(B1), .B0(B0), .P(parity_4bit_generator_1_p));
  xor xor_1 (E, parity_4bit_generator_1_p, P);
endmodule

module decoder_display_7segment (
  input  B0,
  input  B1,
  input  B2,
  input  B3,
  output a,
  output b,
  output c,
  output d,
  output e,
  output f,
  output g
);

  wire and_1_out, and_2_out, and_3_out, and_4_out, and_5_out, and_6_out, and_7_out, and_8_out, and_9_out,
       and_10_out, not_1_out, not_2_out, not_3_out, xnor_1_out, xnor_2_out, xor_1_out;

  not not_1 (not_1_out, B0);
  not not_2 (not_2_out, B1);
  not not_3 (not_3_out, B2);
  xnor xnor_1 (xnor_1_out, B0, B2);
  xnor xnor_2 (xnor_2_out, B1, B0);
  and and_1 (and_1_out, not_1_out, B1);
  and and_2 (and_2_out, B1, not_3_out);
  and and_3 (and_3_out, not_1_out, not_3_out);
  and and_4 (and_4_out, B0, not_2_out, B2);
  and and_5 (and_5_out, not_1_out, B1);
  and and_6 (and_6_out, not_1_out, not_3_out);
  and and_7 (and_7_out, not_2_out, B2);
  and and_8 (and_8_out, not_1_out, not_2_out);
  and and_9 (and_9_out, not_1_out, B2);
  xor xor_1 (xor_1_out, B1, B2);
  and and_10 (and_10_out, not_1_out, B1);
  or or_1 (a, xnor_1_out, B1, B3);
  or or_2 (b, xnor_2_out, not_3_out);
  or or_3 (c, B0, not_2_out, B2);
  or or_4 (d, and_1_out, and_2_out, B3, and_3_out, and_4_out);
  or or_5 (e, and_5_out, and_6_out);
  or or_6 (f, and_7_out, B3, and_8_out, and_9_out);
  or or_7 (g, xor_1_out, B3, and_10_out);

  // Notes on the sheet:
  //   4-bit BCD 7-SegmentDisplayDecoder
endmodule

module simple_adder_machine (
  input  A7,
  input  A6,
  input  A5,
  input  A4,
  input  A3,
  input  A2,
  input  A1,
  input  A0,
  input  B7,
  input  B6,
  input  B5,
  input  B4,
  input  B3,
  input  B2,
  input  B1,
  input  B0
);

  wire bcd_4bit_adder_1_c4, bcd_4bit_adder_1_s0, bcd_4bit_adder_1_s1, bcd_4bit_adder_1_s2,
       bcd_4bit_adder_1_s3, bcd_4bit_adder_2_c4, bcd_4bit_adder_2_s0, bcd_4bit_adder_2_s1,
       bcd_4bit_adder_2_s2, bcd_4bit_adder_2_s3, decoder_display_7segment_1_a, decoder_display_7segment_1_b,
       decoder_display_7segment_1_c, decoder_display_7segment_1_d, decoder_display_7segment_1_e,
       decoder_display_7segment_1_f, decoder_display_7segment_1_g, decoder_display_7segment_2_a,
       decoder_display_7segment_2_b, decoder_display_7segment_2_c, decoder_display_7segment_2_d,
       decoder_display_7segment_2_e, decoder_display_7segment_2_f, decoder_display_7segment_2_g,
       decoder_display_7segment_3_a, decoder_display_7segment_3_b, decoder_display_7segment_3_c,
       decoder_display_7segment_3_d, decoder_display_7segment_3_e, decoder_display_7segment_3_f,
       decoder_display_7segment_3_g, decoder_display_7segment_4_a, decoder_display_7segment_4_b,
       decoder_display_7segment_4_c, decoder_display_7segment_4_d, decoder_display_7segment_4_e,
       decoder_display_7segment_4_f, decoder_display_7segment_4_g, decoder_display_7segment_5_a,
       decoder_display_7segment_5_b, decoder_display_7segment_5_c, decoder_display_7segment_5_d,
       decoder_display_7segment_5_e, decoder_display_7segment_5_f, decoder_display_7segment_5_g,
       decoder_display_7segment_6_a, decoder_display_7segment_6_b, decoder_display_7segment_6_c,
       decoder_display_7segment_6_d, decoder_display_7segment_6_e, decoder_display_7segment_6_f,
       decoder_display_7segment_6_g, decoder_display_7segment_7_a, decoder_display_7segment_7_b,
       decoder_display_7segment_7_c, decoder_display_7segment_7_d, decoder_display_7segment_7_e,
       decoder_display_7segment_7_f, decoder_display_7segment_7_g;

  decoder_display_7segment decoder_display_7segment_1 (
    .B0(A4), .B1(A5), .B2(A6), .B3(A7), .a(decoder_display_7segment_1_a), .b(decoder_display_7segment_1_b),
    .c(decoder_display_7segment_1_c), .d(decoder_display_7segment_1_d), .e(decoder_display_7segment_1_e),
    .f(decoder_display_7segment_1_f), .g(decoder_display_7segment_1_g));
  decoder_display_7segment decoder_display_7segment_2 (
    .B0(A0), .B1(A1), .B2(A2), .B3(A3), .a(decoder_display_7segment_2_a), .b(decoder_display_7segment_2_b),
    .c(decoder_display_7segment_2_c), .d(decoder_display_7segment_2_d), .e(decoder_display_7segment_2_e),
    .f(decoder_display_7segment_2_f), .g(decoder_display_7segment_2_g));
  _7_Segment_Display u_7_segment_display_1 (
    .g(decoder_display_7segment_1_g), .f(decoder_display_7segment_1_f), .a(decoder_display_7segment_1_a),
    .b(decoder_display_7segment_1_b), .e(decoder_display_7segment_1_e), .d(decoder_display_7segment_1_d),
    .c(decoder_display_7segment_1_c), .dp(1'b0));
  _7_Segment_Display u_7_segment_display_2 (
    .g(decoder_display_7segment_2_g), .f(decoder_display_7segment_2_f), .a(decoder_display_7segment_2_a),
    .b(decoder_display_7segment_2_b), .e(decoder_display_7segment_2_e), .d(decoder_display_7segment_2_d),
    .c(decoder_display_7segment_2_c), .dp(1'b0));
  decoder_display_7segment decoder_display_7segment_3 (
    .B0(B4), .B1(B5), .B2(B6), .B3(B7), .a(decoder_display_7segment_3_a), .b(decoder_display_7segment_3_b),
    .c(decoder_display_7segment_3_c), .d(decoder_display_7segment_3_d), .e(decoder_display_7segment_3_e),
    .f(decoder_display_7segment_3_f), .g(decoder_display_7segment_3_g));
  decoder_display_7segment decoder_display_7segment_4 (
    .B0(B0), .B1(B1), .B2(B2), .B3(B3), .a(decoder_display_7segment_4_a), .b(decoder_display_7segment_4_b),
    .c(decoder_display_7segment_4_c), .d(decoder_display_7segment_4_d), .e(decoder_display_7segment_4_e),
    .f(decoder_display_7segment_4_f), .g(decoder_display_7segment_4_g));
  _7_Segment_Display u_7_segment_display_3 (
    .g(decoder_display_7segment_3_g), .f(decoder_display_7segment_3_f), .a(decoder_display_7segment_3_a),
    .b(decoder_display_7segment_3_b), .e(decoder_display_7segment_3_e), .d(decoder_display_7segment_3_d),
    .c(decoder_display_7segment_3_c), .dp(1'b0));
  _7_Segment_Display u_7_segment_display_4 (
    .g(decoder_display_7segment_4_g), .f(decoder_display_7segment_4_f), .a(decoder_display_7segment_4_a),
    .b(decoder_display_7segment_4_b), .e(decoder_display_7segment_4_e), .d(decoder_display_7segment_4_d),
    .c(decoder_display_7segment_4_c), .dp(1'b0));
  bcd_4bit_adder bcd_4bit_adder_1 (
    .Ci(1'b0), .A0(A0), .B0(B0), .A1(A1), .B1(B1), .A2(A2), .B2(B2), .A3(A3), .B3(B3), .GND(1'b0),
    .S0(bcd_4bit_adder_1_s0), .S1(bcd_4bit_adder_1_s1), .S2(bcd_4bit_adder_1_s2), .S3(bcd_4bit_adder_1_s3),
    .C4(bcd_4bit_adder_1_c4));
  bcd_4bit_adder bcd_4bit_adder_2 (
    .Ci(bcd_4bit_adder_1_c4), .A0(A4), .B0(B4), .A1(A5), .B1(B5), .A2(A6), .B2(B6), .A3(A7), .B3(B7),
    .GND(1'b0), .S0(bcd_4bit_adder_2_s0), .S1(bcd_4bit_adder_2_s1), .S2(bcd_4bit_adder_2_s2),
    .S3(bcd_4bit_adder_2_s3), .C4(bcd_4bit_adder_2_c4));
  decoder_display_7segment decoder_display_7segment_5 (
    .B0(bcd_4bit_adder_2_c4), .B1(1'b0), .B2(1'b0), .B3(1'b0), .a(decoder_display_7segment_5_a),
    .b(decoder_display_7segment_5_b), .c(decoder_display_7segment_5_c), .d(decoder_display_7segment_5_d),
    .e(decoder_display_7segment_5_e), .f(decoder_display_7segment_5_f), .g(decoder_display_7segment_5_g));
  decoder_display_7segment decoder_display_7segment_6 (
    .B0(bcd_4bit_adder_2_s0), .B1(bcd_4bit_adder_2_s1), .B2(bcd_4bit_adder_2_s2), .B3(bcd_4bit_adder_2_s3),
    .a(decoder_display_7segment_6_a), .b(decoder_display_7segment_6_b), .c(decoder_display_7segment_6_c),
    .d(decoder_display_7segment_6_d), .e(decoder_display_7segment_6_e), .f(decoder_display_7segment_6_f),
    .g(decoder_display_7segment_6_g));
  decoder_display_7segment decoder_display_7segment_7 (
    .B0(bcd_4bit_adder_1_s0), .B1(bcd_4bit_adder_1_s1), .B2(bcd_4bit_adder_1_s2), .B3(bcd_4bit_adder_1_s3),
    .a(decoder_display_7segment_7_a), .b(decoder_display_7segment_7_b), .c(decoder_display_7segment_7_c),
    .d(decoder_display_7segment_7_d), .e(decoder_display_7segment_7_e), .f(decoder_display_7segment_7_f),
    .g(decoder_display_7segment_7_g));
  _7_Segment_Display u_7_segment_display_5 (
    .g(decoder_display_7segment_5_g), .f(decoder_display_7segment_5_f), .a(decoder_display_7segment_5_a),
    .b(decoder_display_7segment_5_b), .e(decoder_display_7segment_5_e), .d(decoder_display_7segment_5_d),
    .c(decoder_display_7segment_5_c), .dp(1'b0));
  _7_Segment_Display u_7_segment_display_6 (
    .g(decoder_display_7segment_7_g), .f(decoder_display_7segment_7_f), .a(decoder_display_7segment_7_a),
    .b(decoder_display_7segment_7_b), .e(decoder_display_7segment_7_e), .d(decoder_display_7segment_7_d),
    .c(decoder_display_7segment_7_c), .dp(1'b0));
  _7_Segment_Display u_7_segment_display_7 (
    .g(decoder_display_7segment_6_g), .f(decoder_display_7segment_6_f), .a(decoder_display_7segment_6_a),
    .b(decoder_display_7segment_6_b), .e(decoder_display_7segment_6_e), .d(decoder_display_7segment_6_d),
    .c(decoder_display_7segment_6_c), .dp(1'b0));

  // Notes on the sheet:
  //   Operando 1:
  //   Operando 2:
  //   Resultado:
endmodule
