// Logisim project clock.circ as structural Verilog: 7 circuits, main circuit main
module main (
  input  RST
);

  wire CLK_out;
  wire [7:0] counter_time_1_hh, counter_time_1_mm, counter_time_1_ss;

  Clock CLK (.out(CLK_out));
  counter_time counter_time_1 (
    .CLK(CLK_out), .RST(RST), .HH(counter_time_1_hh), .MM(counter_time_1_mm), .SS(counter_time_1_ss));
  Hex_Digit_Display hex_digit_display_1 (.value(counter_time_1_hh[7:4]));  // open: dp
  Hex_Digit_Display hex_digit_display_2 (.value(counter_time_1_hh[3:0]));  // open: dp
  Hex_Digit_Display hex_digit_display_3 (.value(counter_time_1_mm[7:4]));  // open: dp
  Hex_Digit_Display hex_digit_display_4 (.value(counter_time_1_mm[3:0]));  // open: dp
  Hex_Digit_Display hex_digit_display_5 (.value(counter_time_1_ss[7:4]));  // open: dp
  Hex_Digit_Display hex_digit_display_6 (.value(counter_time_1_ss[3:0]));  // open: dp
endmodule

module counter_mod_3 (
  input  CLK,
  input  RST,
  output Q1,
  output Q0
);

  wire and_1_out, R0_qn, R1_qn;

  and and_1 (and_1_out, R0_qn, R1_qn);
  D_Flip_Flop R1 (.D(Q0), .clk(CLK), .Q(Q1), .Qn(R1_qn), .reset(RST));  // open: preset
  D_Flip_Flop R0 (.D(and_1_out), .clk(CLK), .Q(Q0), .Qn(R0_qn), .reset(RST));  // open: preset
endmodule

module counter_mod_6 (
  input  CLK,
  input  RST,
  output Q2,
  output Q1,
  output Q0
);

  wire and_1_out, and_2_out, and_3_out, and_4_out, or_1_out, or_2_out, R0_qn, R1_qn, R2_qn;

  and and_1 (and_1_out, Q2, R0_qn);
  and and_2 (and_2_out, Q1, Q0);
  and and_3 (and_3_out, R2_qn, R1_qn, Q0);
  and and_4 (and_4_out, Q1, R0_qn);
  or or_1 (or_1_out, and_1_out, and_2_out);
  or or_2 (or_2_out, and_3_out, and_4_out);
  D_Flip_Flop R2 (.D(or_1_out), .clk(CLK), .Q(Q2), .Qn(R2_qn), .reset(RST));  // open: preset
  D_Flip_Flop R1 (.D(or_2_out), .clk(CLK), .Q(Q1), .Qn(R1_qn), .reset(RST));  // open: preset
  D_Flip_Flop R0 (.D(R0_qn), .clk(CLK), .Q(Q0), .Qn(R0_qn), .reset(RST));  // open: preset

  // Notes on the sheet:
  //   Q0
  //   Q1
  //   Q2
endmodule

module counter_mod_10 (
  input  CLK,
  input  RST,
  output Q3,
  output Q2,
  output Q1,
  output Q0
);

  wire and_1_out, and_2_out, and_3_out, and_4_out, and_5_out, and_6_out, and_7_out, or_1_out, or_2_out,
       or_3_out, R0_qn, R1_qn, R2_qn, R3_qn;

  and and_1 (and_1_out, Q3, R0_qn);
  and and_2 (and_2_out, Q2, Q1, Q0);
  and and_3 (and_3_out, R2_qn, Q1, Q0);
  and and_4 (and_4_out, Q2, R0_qn);
  and and_5 (and_5_out, Q2, R1_qn);
  and and_6 (and_6_out, R3_qn, R1_qn, Q0);
  and and_7 (and_7_out, Q1, R0_qn);
  or or_1 (or_1_out, and_1_out, and_2_out);
  or or_2 (or_2_out, and_3_out, and_4_out, and_5_out);
  or or_3 (or_3_out, and_6_out, and_7_out);
  D_Flip_Flop R3 (.D(or_1_out), .clk(CLK), .Q(Q3), .Qn(R3_qn), .reset(RST));  // open: preset
  D_Flip_Flop R2 (.D(or_2_out), .clk(CLK), .Q(Q2), .Qn(R2_qn), .reset(RST));  // open: preset
  D_Flip_Flop R1 (.D(or_3_out), .clk(CLK), .Q(Q1), .Qn(R1_qn), .reset(RST));  // open: preset
  D_Flip_Flop R0 (.D(R0_qn), .clk(CLK), .Q(Q0), .Qn(R0_qn), .reset(RST));  // open: preset

  // Notes on the sheet:
  //   Q0
  //   Q1
  //   Q2
  //   Q3
endmodule

module counter_mod_24 (
  input  CLK,
  input  RST,
  output Q5,
  output Q4,
  output Q3,
  output Q2,
  output Q1,
  output Q0
);

  wire not_1_out, or_1_out, RST_TIME;

  not not_1 (not_1_out, Q3);
  or or_1 (or_1_out, RST, RST_TIME);
  counter_mod_3 counter_mod_3_1 (.CLK(not_1_out), .RST(or_1_out), .Q1(Q5), .Q0(Q4));
  counter_mod_10 counter_mod_10_1 (.CLK(CLK), .RST(or_1_out), .Q3(Q3), .Q2(Q2), .Q1(Q1), .Q0(Q0));
  and and_1 (RST_TIME, Q5, Q2);
endmodule

module counter_mod_60 (
  input  CLK,
  input  RST,
  output Q6,
  output Q5,
  output Q4,
  output Q3,
  output Q2,
  output Q1,
  output Q0
);

  wire not_1_out;

  not not_1 (not_1_out, Q3);
  counter_mod_6 counter_mod_6_1 (.CLK(not_1_out), .RST(RST), .Q2(Q6), .Q1(Q5), .Q0(Q4));
  counter_mod_10 counter_mod_10_1 (.CLK(CLK), .RST(RST), .Q3(Q3), .Q2(Q2), .Q1(Q1), .Q0(Q0));
endmodule

module counter_time (
  input  CLK,
  input  RST,
  output [7:0] HH,
  output [7:0] MM,
  output [7:0] SS
);

  wire not_1_out, not_2_out;

  not not_1 (not_1_out, MM[6]);
  not not_2 (not_2_out, SS[6]);
  counter_mod_24 counter_mod_24_1 (
    .CLK(not_1_out), .RST(RST), .Q5(HH[5]), .Q4(HH[4]), .Q3(HH[3]), .Q2(HH[2]), .Q1(HH[1]), .Q0(HH[0]));
  counter_mod_60 counter_mod_60_1 (
    .CLK(not_2_out), .RST(RST), .Q6(MM[6]), .Q5(MM[5]), .Q4(MM[4]), .Q3(MM[3]), .Q2(MM[2]), .Q1(MM[1]),
    .Q0(MM[0]));
  counter_mod_60 counter_mod_60_2 (
    .CLK(CLK), .RST(RST), .Q6(SS[6]), .Q5(SS[5]), .Q4(SS[4]), .Q3(SS[3]), .Q2(SS[2]), .Q1(SS[1]), .Q0(SS[0]));

  assign HH[7:6] = 2'b00;
  assign MM[7] = 1'b0;
  assign SS[7] = 1'b0;
endmodule
