// Logisim project register.circ as structural Verilog: 1 circuit, main circuit main
module main (
  input  D3_IN,
  input  D2_IN,
  input  D1_IN,
  input  D0_IN,
  input  PRESET,
  input  SERIAL_IN,
  input  RESET,
  input  in_8,
  input  in_9,
  input  in_10,
  input  in_11,
  output Serial_Out,
  output out_13,
  output out_14,
  output out_15,
  output out_16
);

  wire CLK_out, multiplexer_1_out, multiplexer_2_out, multiplexer_3_out, multiplexer_4_out,
       multiplexer_5_out, multiplexer_6_out, multiplexer_7_out, multiplexer_8_out, multiplexer_9_out,
       multiplexer_10_out;

  Clock CLK (.out(CLK_out));
  Multiplexer multiplexer_1 (.in0(SERIAL_IN), .in1(out_16), .out(multiplexer_1_out), .sel(in_8));
  Multiplexer multiplexer_2 (.in0(D3_IN), .in1(multiplexer_1_out), .out(multiplexer_2_out), .sel(in_9));
  Multiplexer multiplexer_3 (.in0(out_14), .in1(multiplexer_2_out), .out(multiplexer_3_out), .sel(in_10));
  D_Flip_Flop d_ff_1 (.D(multiplexer_3_out), .clk(CLK_out), .Q(out_13), .preset(PRESET), .reset(RESET));  // open: Qn
  Multiplexer multiplexer_4 (.in0(D2_IN), .in1(out_13), .out(multiplexer_4_out), .sel(in_9));
  D_Flip_Flop d_ff_2 (.D(multiplexer_5_out), .clk(CLK_out), .Q(out_14), .preset(PRESET), .reset(RESET));  // open: Qn
  Multiplexer multiplexer_5 (.in0(out_15), .in1(multiplexer_4_out), .out(multiplexer_5_out), .sel(in_10));
  Multiplexer multiplexer_6 (.in0(D1_IN), .in1(out_14), .out(multiplexer_6_out), .sel(in_9));
  D_Flip_Flop d_ff_3 (.D(multiplexer_7_out), .clk(CLK_out), .Q(out_15), .preset(PRESET), .reset(RESET));  // open: Qn
  Multiplexer multiplexer_7 (.in0(out_16), .in1(multiplexer_6_out), .out(multiplexer_7_out), .sel(in_10));
  Multiplexer multiplexer_8 (.in0(D0_IN), .in1(out_15), .out(multiplexer_8_out), .sel(in_9));
  Multiplexer multiplexer_9 (.in0(1'b0), .in1(out_13), .out(multiplexer_9_out), .sel(in_11));
  D_Flip_Flop d_ff_4 (.D(multiplexer_10_out), .clk(CLK_out), .Q(out_16), .preset(PRESET), .reset(RESET));  // open: Qn
  Multiplexer multiplexer_10 (.in0(multiplexer_9_out), .in1(multiplexer_8_out), .out(multiplexer_10_out), .sel(in_10));

  assign Serial_Out = out_16;

  // Notes on the sheet:
  //   SERIAL/RROT
  //   P'/S
  //   L'/R
  //   D3_OUT
  //   D2_OUT
  //   D1_OUT
  //   LROT
  //   D0_OUT
endmodule
