// Logisim project voting_system_v1.circ as structural Verilog: 1 circuit, main circuit main
module main (
);

  wire and_1_out, and_2_out, button_1_out, button_2_out, button_3_out, button_4_out, button_5_out, d_ff_1_q,
       d_ff_2_q, d_ff_3_q, d_ff_4_q, or_1_out, or_2_out;

  Button button_1 (.out(button_1_out));
  Button button_2 (.out(button_2_out));
  Button button_3 (.out(button_3_out));
  Button button_4 (.out(button_4_out));
  Button button_5 (.out(button_5_out));
  D_Flip_Flop d_ff_1 (.D(button_5_out), .clk(button_5_out), .Q(d_ff_1_q), .reset(button_1_out));  // open: Qn, preset
  D_Flip_Flop d_ff_2 (.D(button_4_out), .clk(button_4_out), .Q(d_ff_2_q), .reset(button_1_out));  // open: Qn, preset
  D_Flip_Flop d_ff_3 (.D(button_3_out), .clk(button_3_out), .Q(d_ff_3_q), .reset(button_1_out));  // open: Qn, preset
  D_Flip_Flop d_ff_4 (.D(button_2_out), .clk(button_2_out), .Q(d_ff_4_q), .reset(button_1_out));  // open: Qn, preset
  or or_1 (or_1_out, d_ff_1_q, d_ff_2_q, d_ff_3_q);
  and and_1 (and_1_out, d_ff_3_q, d_ff_2_q, d_ff_1_q);
  and and_2 (and_2_out, or_1_out, d_ff_4_q);
  or or_2 (or_2_out, and_2_out, and_1_out);
  LED led_1 (.in(or_2_out));

  // Notes on the sheet:
  //   Reset
  //   P
  //   D
  //   T
  //   S
endmodule
