// Logisim project voting_system_v3.circ as structural Verilog: 1 circuit, main circuit main
module main (
);

  wire button_1_out, button_2_out, button_3_out, button_4_out, button_5_out, nand_1_out, nand_2_out,
       nand_3_out, nand_4_out, nand_5_out, nand_6_out, nand_7_out, t_ff_1_q, t_ff_2_q, t_ff_3_q, t_ff_4_q;

  Button button_1 (.out(button_1_out));
  Button button_2 (.out(button_2_out));
  Button button_3 (.out(button_3_out));
  Button button_4 (.out(button_4_out));
  Button button_5 (.out(button_5_out));
  T_Flip_Flop t_ff_1 (.T(button_5_out), .clk(button_5_out), .Q(t_ff_1_q), .reset(button_1_out));  // open: Qn, preset
  T_Flip_Flop t_ff_2 (.T(button_4_out), .clk(button_4_out), .Q(t_ff_2_q), .reset(button_1_out));  // open: Qn, preset
  T_Flip_Flop t_ff_3 (.T(button_3_out), .clk(button_3_out), .Q(t_ff_3_q), .reset(button_1_out));  // open: Qn, preset
  T_Flip_Flop t_ff_4 (.T(button_2_out), .clk(button_2_out), .Q(t_ff_4_q), .reset(button_1_out));  // open: Qn, preset
  nand nand_1 (nand_1_out, t_ff_1_q, t_ff_3_q);
  nand nand_2 (nand_2_out, t_ff_1_q, t_ff_4_q);
  nand nand_3 (nand_3_out, t_ff_3_q, t_ff_4_q);
  nand nand_4 (nand_4_out, t_ff_2_q, t_ff_4_q);
  nand nand_5 (nand_5_out, nand_1_out, nand_1_out);
  nand nand_6 (nand_6_out, t_ff_2_q, nand_5_out);
  nand nand_7 (nand_7_out, nand_6_out, nand_2_out, nand_3_out, nand_4_out);
  LED led_1 (.in(nand_7_out));

  // Notes on the sheet:
  //   Reset
  //   P
  //   D
  //   T
  //   S
endmodule
